# Fritzing sketch RC Car Wiring Fritzing File (saved by Fritzing 0.9.3b)

parts:
  Part1 = Arduino Uno (Rev3)
  S1 = H-Bridge with L298N
  Part2 = HC-05 [part_number=HC-05 package="breakout board"]
  M1 = DC Motor
  M2 = DC Motor
  U2 = LIPO-2000mAh [package=lipo-2000]

nets:
  N1: Part1.D8, S1.IN2
  N2: Part1.D9_PWM, S1.IN1
  N3: Part1.D10_PWM/SS, S1.ENA
  N4: Part1.D0/RX, Part2.TXD
  N5: Part1.D1/TX, Part2.RXD
  N6: Part1.D5_PWM, S1.ENB
  N7: Part1.D6_PWM, S1.IN4
  N8: Part1.D7, S1.IN3
  5V: Part1.5V, Part2.VCC
  GND: Part1.GND, S1.GND, Part2.GND, U2.-
  VIN: Part1.VIN, S1.5V
  N9: S1.12V, U2.+
  N10: S1.M1-01, M2.pin_2
  N11: S1.M1-02, M2.pin_1
  N12: S1.M2-01, M1.pin_2
  N13: S1.M2-02, M1.pin_1

custom parts:
  H-Bridge with L298N: h-bridge
  HC-05: A commonly available HC-05 Bluetooth breakout board.
